// Logisim project Etapa1.circ as structural Verilog: 1 circuit, main circuit main
module main (
  input  A,
  input  B,
  input  C,
  input  D,
  input  E,
  input  in_6,
  output [8:0] SALIDA
);

  wire clock_1_out, undriven;
  wire [2:0] undriven_2;

  Clock clock_1 (.out(clock_1_out));
  Counter #(.max('h7), .width(3)) counter_1 (
    .load(undriven), .up(1'b1), .clk(clock_1_out), .Q(SALIDA[2:0]));  // open: clr, count, D, carry
  Multiplexer multiplexer_1 ();  // open: in0, in1, out, sel
  ROM #(.addrWidth(3), .dataWidth(3)) rom_1 (.addr(undriven_2));  // open: data
  not not_1 (SALIDA[8], in_6);

  assign SALIDA[7:3] = {5{in_6}};
endmodule
